# Fritzing sketch Blink once to accept (saved by Fritzing 0.9.3b)
breadboards: 1

parts:
  Part1 = Arduino Nano (Rev3.0)
  R1 = Resistor [tolerance=±5% resistance=220 package="0402 [SMD]"]
  R2 = Resistor [tolerance=±5% resistance=220 package="0402 [SMD]"]
  LED1 = smd LED [color="Red (633nm)" package="0603 [SMD]"]
  LED2 = smd LED [color="Red (633nm)" package="0603 [SMD]"]

nets:
  N1: Part1.GND, LED1.cathode, LED2.cathode
  N2: Part1.D12/MISO, R1.Pin_0
  N3: Part1.D13/SCK, R2.Pin_0
  N4: R1.Pin_1, LED1.anode
  N5: R2.Pin_1, LED2.anode
