# Fritzing sketch count_me_in (saved by Fritzing 0.9.3b)
breadboards: 1

parts:
  Part1 = Arduino Nano (Rev3.0) (ICSP)
  R1 = Resistor [tolerance=±5% resistance=220 package=THT]
  LED1 = 2-digit 7-segment [package=THT-longpads]
  R2 = Resistor [tolerance=±5% resistance=220 package=THT]
  R3 = Resistor [tolerance=±5% resistance=220 package=THT]
  R4 = Resistor [tolerance=±5% resistance=220 package=THT]
  R5 = Resistor [tolerance=±5% resistance=220 package=THT]
  R6 = Resistor [tolerance=±5% resistance=220 package=THT]
  R7 = Resistor [tolerance=±5% resistance=220 package=THT]
  R8 = Resistor [tolerance=±5% resistance=220 package=THT]
  R9 = Resistor [tolerance=±5% resistance=220 package=THT]
  R10 = Resistor [tolerance=±5% resistance=220 package=THT]
  R11 = Resistor [tolerance=±5% resistance=220 package=THT]
  R12 = Resistor [tolerance=±5% resistance=220 package=THT]
  R13 = Resistor [tolerance=±5% resistance=220 package=THT]
  R14 = Resistor [tolerance=±5% resistance=220 package=THT]
  R15 = Resistor [tolerance=±5% resistance=220 package=THT]

nets:
  N1: Part1.D2, R14.Pin_0
  N2: Part1.D3, R13.Pin_0
  N3: Part1.D4, R12.Pin_0
  N4: Part1.D5, R11.Pin_0
  N5: Part1.D6, R10.Pin_0
  N6: Part1.D7, R9.Pin_0
  N7: Part1.D8, R8.Pin_0
  N8: Part1.D9, R7.Pin_1
  N9: Part1.D10, R6.Pin_0
  N10: Part1.D11/MOSI, R5.Pin_0
  N11: Part1.D12/MISO, R4.Pin_1
  N12: Part1.5V, R15.Pin_1
  N13: Part1.A5, R3.Pin_0
  N14: Part1.A4, R2.Pin_0
  N15: Part1.D13/SCK, R1.Pin_0
  N16: R1.Pin_1, LED1.DIG2, LED1.DIG1, R15.Pin_0
  N17: LED1.A, R12.Pin_1
  N18: LED1.E, R5.Pin_1
  N19: LED1.D, R3.Pin_1
  N20: LED1.G, R7.Pin_0
  N21: LED1.F, R10.Pin_1
  N22: LED1.B, R11.Pin_1

custom parts:
  2-digit 7-segment: Most common two-digit seven-segment led indicator you can find on the internet. 10 legs: 2 common electrodes (one per each digit), 8 electrodes of each segment.
