# Fritzing sketch To die or not to die (saved by Fritzing 0.9.3b)
breadboards: 1

parts:
  Part1 = Arduino Nano (Rev3.0) (ICSP)
  R1 = Resistor [tolerance=±5% resistance=220 package="2010 [SMD]"]
  LED1 = smd LED [color="Red (633nm)" package="0805 [SMD]"]
  LED2 = smd LED [color="Red (633nm)" package="0805 [SMD]"]
  LED3 = smd LED [color="Red (633nm)" package="0805 [SMD]"]
  LED4 = smd LED [color="Red (633nm)" package="0805 [SMD]"]
  LED5 = smd LED [color="Red (633nm)" package="0805 [SMD]"]
  LED6 = smd LED [color="Red (633nm)" package="0805 [SMD]"]
  LED7 = smd LED [color="Red (633nm)" package="0805 [SMD]"]
  LED8 = smd LED [color="Red (633nm)" package="0805 [SMD]"]
  LED9 = smd LED [color="Red (633nm)" package="0805 [SMD]"]
  R2 = Resistor [tolerance=±5% resistance=220 package="2010 [SMD]"]
  R3 = Resistor [tolerance=±5% resistance=220 package="2010 [SMD]"]
  R4 = Resistor [tolerance=±5% resistance=220 package="2010 [SMD]"]
  R5 = Resistor [tolerance=±5% resistance=220 package="2010 [SMD]"]
  R6 = Resistor [tolerance=±5% resistance=220 package="2010 [SMD]"]
  R7 = Resistor [tolerance=±5% resistance=220 package="2010 [SMD]"]
  R8 = Resistor [tolerance=±5% resistance=220 package="2010 [SMD]"]
  R10 = Resistor [tolerance=±5% resistance=220 package="2010 [SMD]"]
  S1 = Pushbutton [package="[THT]"]
  R11 = Resistor [tolerance=±5% resistance=220 package="2010 [SMD]"]

nets:
  N1: Part1.GND, R1.Pin_1, LED1.cathode, LED1.anode, LED2.cathode, LED3.cathode, LED4.cathode, LED5.cathode, LED6.cathode, LED6.anode, LED7.cathode, LED8.cathode, LED9.cathode, R4.Pin_0, R10.Pin_1, S1.Pin_1, S1.Pin_2, S1.Pin_3, S1.Pin_4
  N2: Part1.D2, R11.Pin_0
  N3: Part1.D3, R8.Pin_0
  N4: Part1.D4, R7.Pin_0
  N5: Part1.D5, R6.Pin_0
  N6: Part1.D6, R5.Pin_0
  N7: Part1.D7, R4.Pin_1
  N8: Part1.D10, R3.Pin_0
  N9: Part1.D11/MOSI, R2.Pin_0
  N10: Part1.D12/MISO, R1.Pin_0
  N11: Part1.A0, R10.Pin_0
  N12: LED2.anode, R2.Pin_1
  N13: LED3.anode, R3.Pin_1
  N14: LED4.anode, R5.Pin_1
  N15: LED5.anode, R6.Pin_1
  N16: LED7.anode, R7.Pin_1
  N17: LED8.anode, R8.Pin_1
  N18: LED9.anode, R11.Pin_1
