# Fritzing sketch ADC baby (saved by Fritzing 0.9.3b)
breadboards: 1

parts:
  Part1 = Arduino Nano (Rev3.0)
  R1 = Resistor [tolerance=±5% resistance=220 package="2010 [SMD]"]
  R2 = Resistor [tolerance=±5% resistance=220 package="2010 [SMD]"]
  SP1 = SPEAKER [package=pcb_mount_speaker]
  R3 = Rotary Potentiometer (Small) [maximum_resistance=100kΩ package=THT]

nets:
  N1: Part1.GND, R1.Pin_1, SP1.+, SP1.-
  N2: Part1.D8, R1.Pin_0
  N3: Part1.5V, R2.Pin_0
  N4: Part1.A0, R3.wiper
  N5: R2.Pin_1, R3.leg1, R3.leg2
