# Fritzing sketch Led there be light (saved by Fritzing 0.9.3b)
breadboards: 1

parts:
  Part1 = Arduino Nano (Rev3.0)
  LED1 = RGB LED (com. anode, rbg) [package="5 mm [THT]"]
  R1 = Resistor [tolerance=±5% resistance=220 package="2512 [SMD]"]
  R2 = Resistor [tolerance=±5% resistance=220 package="2512 [SMD]"]
  R3 = Resistor [tolerance=±5% resistance=220 package="2512 [SMD]"]
  R4 = Resistor [tolerance=±5% resistance=220 package="2512 [SMD]"]

nets:
  N1: Part1.D9, R2.Pin_1
  N2: Part1.D10, R3.Pin_1
  N3: Part1.D11/MOSI, R4.Pin_1
  N4: Part1.5V, R1.Pin_0
  N5: LED1.red_cathode, R4.Pin_0
  N6: LED1.common_anode, R3.Pin_0
  N7: LED1.blue_cathode, R1.Pin_1
  N8: LED1.green_cathode, R2.Pin_0
