# Fritzing sketch ET Phone home (saved by Fritzing 0.9.3b)
breadboards: 1

parts:
  Onderdeel1 = Arduino Nano (Rev3.0) (ICSP)
  LCD1 = LCD screen
  U1 = POT [package=pot_alpha_rv16af-20]
  R1 = Resistor [tolerance=±5% resistance=220 package="2010 [SMD]"]

nets:
  GND: Onderdeel1.GND, LCD1.VSS, LCD1.R/W, LCD1.LED-, U1.E
  N1: Onderdeel1.D2, LCD1.DB7
  N2: Onderdeel1.D3, LCD1.DB6
  N3: Onderdeel1.D4, LCD1.DB5
  N4: Onderdeel1.D5, LCD1.DB4
  N5: Onderdeel1.D11/MOSI, LCD1.E
  N6: Onderdeel1.D12/MISO, LCD1.RS
  N7: Onderdeel1.5V, R1.Pin_1
  N8: LCD1.VDD, LCD1.LED+, U1.A, R1.Pin_0
  N9: LCD1.V0, U1.S
