# Fritzing sketch END. Show your moves (saved by Fritzing 0.9.3b)
breadboards: 2

parts:
  Part1 = Arduino Nano (Rev3.0) (ICSP)
  74HC139N2 = 74HC139N [part_number=74HC139N package="DIP (Dual Inline) [THT]"]
  DS1 = DS18B20 1-Wire Temperature Sensor [part_number=DS18B20]  # not connected
  D1 = LED_BARGRAPH_10 [package=led_bargaph_10]
  LED1 = smd LED [color="Red (633nm)" package="1206 [SMD]"]
  LED2 = LED - 5mm [color="Red (633nm)" package="5 mm [THT]"]
  LED3 = smd LED [color="Red (633nm)" package="1206 [SMD]"]
  S1 = Pushbutton [package="[SMD]"]
  R1 = Resistor [tolerance=±5% resistance=220 package=THT]
  R2 = Resistor [tolerance=±5% resistance=220 package=THT]
  R3 = Resistor [tolerance=±5% resistance=220 package=THT]
  R4 = Resistor [tolerance=±5% resistance=220 package=THT]
  R5 = Resistor [tolerance=±5% resistance=220 package=THT]
  R6 = Resistor [tolerance=±5% resistance=220 package=THT]
  R7 = Resistor [tolerance=±5% resistance=220 package=THT]
  R8 = Resistor [tolerance=±5% resistance=220 package=THT]
  R9 = Resistor [tolerance=±5% resistance=220 package=THT]
  R10 = Resistor [tolerance=±5% resistance=220 package=THT]
  R11 = Resistor [tolerance=±5% resistance=220 package=THT]
  R12 = Resistor [tolerance=±5% resistance=220 package=THT]
  R13 = Resistor [tolerance=±5% resistance=220 package=THT]
  R14 = Resistor [tolerance=±5% resistance=220 package=THT]
  R15 = Resistor [tolerance=±5% resistance=220 package=THT]

nets:
  GND: Part1.GND, 74HC139N2.1A, 74HC139N2.GND, 74HC139N2.2Y2, 74HC139N2.2G_, D1.J_C, D1.I_C, D1.H_C, D1.G_C, D1.F_C, D1.E_C, D1.D_C, D1.C_C, D1.B_C, D1.A_C, LED1.cathode, LED2.cathode, LED3.cathode, S1.Pin_3, S1.Pin_4, R5.Pin_1
  N1: Part1.D2, R6.Pin_0
  N2: Part1.D3, R7.Pin_0
  N3: Part1.D4, R3.Pin_0
  N4: Part1.D5, R2.Pin_0
  N5: Part1.D6, R1.Pin_0
  N6: Part1.D7, R4.Pin_0
  N7: Part1.D10, 74HC139N2.1B
  N8: Part1.D11/MOSI, 74HC139N2.2Y3
  N9: Part1.5V, R5.Pin_0
  N10: Part1.A0, S1.Pin_1, S1.Pin_2
  N11: Part1.3V3, R1.Pin_1
  N12: 74HC139N2.1Y0, R15.Pin_0
  N13: 74HC139N2.1Y1, R14.Pin_0
  N14: 74HC139N2.1Y2, R13.Pin_0
  N15: 74HC139N2.1Y3, R12.Pin_0
  N16: 74HC139N2.2Y1, R11.Pin_0
  N17: 74HC139N2.2Y0, R10.Pin_0
  N18: 74HC139N2.2B, R9.Pin_0
  N19: 74HC139N2.2A, R8.Pin_0
  N20: D1.A_A, R6.Pin_1
  N21: D1.B_A, R7.Pin_1
  N22: D1.C_A, R8.Pin_1
  N23: D1.D_A, R9.Pin_1
  N24: D1.E_A, R10.Pin_1
  N25: D1.F_A, R11.Pin_1
  N26: D1.G_A, R12.Pin_1
  N27: D1.H_A, R13.Pin_1
  N28: D1.I_A, R14.Pin_1
  N29: D1.J_A, R15.Pin_1
  N30: LED1.anode, R2.Pin_1
  N31: LED2.anode, R3.Pin_1
  N32: LED3.anode, R4.Pin_1
